# Fritzing sketch LinearActuatorWiring (saved by Fritzing 0.9.3b)
breadboards: 1

parts:
  Part1 = Arduino Mega 2560 (Rev3)
  S1 = Pushbutton [package="[SMD]"]
  R2 = Resistor [tolerance=±5% resistance=100 package="2010 [SMD]"]
  C2 = Capacitor [package=cap-pth-small2]
  R3 = Resistor [tolerance=±5% resistance=100 package="2010 [SMD]"]
  R6 = Rotary Potentiometer (Large) [maximum_resistance=10kΩ package=THT]
  MD03A1 = Dual VNH2SP30 Motor Driver [part_number=MD03A]
  M1 = DC Motor

nets:
  N1: Part1.A0, R6.wiper
  N2: Part1.D18/TX1, R2.Pin_1
  N3: Part1.GND, S1.Pin_1, S1.Pin_2, S1.Pin_3, S1.Pin_4, R2.Pin_0, C2.1, C2.2, R3.Pin_0, R6.leg1, MD03A1.GND#136, MD03A1.GND#138
  N4: Part1.D11_PWM, MD03A1.1INb
  N5: Part1.D10_PWM, MD03A1.1INa
  N6: Part1.5V, R3.Pin_1, R6.leg2, MD03A1.+5V_(IN)
  N7: Part1.D44, MD03A1.PWM
  N8: MD03A1.OUT_1A, M1.pin_1
  N9: MD03A1.OUT_1B, M1.pin_2

notes:
  A Linear actuator is just a geared DC motor with a potentiometer that specifies the position. This is just a placeholder but it is the same wiring on the actuator.
  I made the wire colors the same as it is on the linear actuators
  This goes to a 12v power supply that can supply at least 5 Amps
  We use a shield that is a single motor driver. It uses the same IC, and most importantly the same pin labels but of course it only has one not two drivers. The pins may move around but they are labeled the exact same way so just connect them as shown
